# Fritzing sketch bb_altimeter (saved by Fritzing 0.8.3b)
breadboards: 1

parts:
  BeagleBone1 = beaglebone-a5
  U1 = MPL3115A2 [package=lga8]

nets:
  N1: BeagleBone1.connectorp9-1, U1.GND
  N2: BeagleBone1.connectorp9-3, U1.VDD, U1.VDDIO
  N3: BeagleBone1.connectorp9-17, U1.SCL
  N4: BeagleBone1.connectorp9-18, U1.SDA
