# Fritzing sketch bb_sharp_ir (saved by Fritzing 0.8.3b)
breadboards: 1

parts:
  J1 = Infrared Proximity Sensor
  BeagleBone1 = BeagleBone Black

nets:
  N1: J1.Vout, BeagleBone1.no_name_yet#40
  N2: J1.GND, BeagleBone1.no_name_yet#1
  N3: J1.Vcc, BeagleBone1.no_name_yet#3

custom parts:
  BeagleBone Black: BeagleBone Black rev. A5B
