# Fritzing sketch bb_dc_motors (saved by Fritzing 0.8.3b)
breadboards: 1

parts:
  M1 = DC Motor
  IC1 = H-Bridge [package=THT]
  BeagleBone1 = beaglebone-a5

nets:
  N1: M1.pin_1, M1.pin_2, IC1.2Y, IC1.2A, IC1.VCC2
  N2: IC1.1_2EN, IC1.1A, IC1.1Y, BeagleBone1.connectorp9-1
  N3: IC1.3_4EN, IC1.3A, IC1.3Y
  N4: IC1.4Y, IC1.4A, IC1.VCC1, BeagleBone1.connectorp9-3, BeagleBone1.connectorp9-17, BeagleBone1.connectorp9-18

notes:
  H-Bridge, we used the TI DRV8837
