# Fritzing sketch bb_mpu9150 (saved by Fritzing 0.8.3b)
breadboards: 1

parts:
  Parte1 = Triple Axis Gyro Breakout ITG-3200
  BeagleBone1 = BeagleBone Black

nets:
  N1: Parte1.VCC, Parte1.VLOGIC, BeagleBone1.no_name_yet#3
  N2: Parte1.GND, Parte1.CLKIN, BeagleBone1.no_name_yet#1
  N3: Parte1.SDA, BeagleBone1.no_name_yet#22
  N4: Parte1.SCL, BeagleBone1.no_name_yet#21

custom parts:
  BeagleBone Black: BeagleBone Black rev. A5B
